# Fritzing sketch iot (saved by Fritzing 0.9.5d)

parts:
  Mod1 = KY-026 Flame Sensor Module [package="Breakout board"]
  DHT1 = DHT11 Humitidy and Temperature Sensor (3 pins)
  module1 = MQ-2 Gas Sensor
  U2 = ESP8266 NodeMCU LoLin base
  J1 = Piezo Speaker  # not connected
  U3 = ESP8266 NodeMCU LoLin module  # not connected

nets:
  GND: Mod1.G, DHT1.Gnd, module1.GND, U2.GND3-2, U2.GND8-8, U2.GND8-9, U2.GND8-11
  N1: Mod1.+, U2.5V-0, U2.5V-2
  N2: Mod1.D0, U2.D0-0
  N3: DHT1.Plus, module1.VCC, U2.3V3-0, U2.3V3-2, U2.3V4
  N4: DHT1.Signal, U2.D2-0, U2.D2-3
  N5: module1.AO, U2.A0

custom parts:
  KY-026 Flame Sensor Module: KY-026 Flame Sensor Module reacts in the presence of fire.
  DHT11 Humitidy and Temperature Sensor (3 pins): DHT11 Humidity and Temperature Sensor (3 pins).
  MQ-2 Gas Sensor: MQ-2 Gas Sensor module of ZHIYU Sensor Kit
  ESP8266 NodeMCU LoLin base: ESP8266 based NodeMCU Base
  ESP8266 NodeMCU LoLin module: ESP8266 based NodeMCU
